// Logisim project stack_logical_normal.circ as structural Verilog: 20 circuits, main circuit d_trigger
module main (
  input  CLK,
  input  RESET,
  input  [1:0] COMMAND,
  input  [2:0] INDEX,
  input  [3:0] IO_DATA_in,
  output [3:0] d0,
  output [3:0] d1,
  output [3:0] d2,
  output [3:0] d3,
  output [3:0] d4,
  output [3:0] IO_DATA_out
);

  stack stack_1 (
    .CLK(CLK), .RESET(RESET), .COMMAND(COMMAND), .INDEX(INDEX), .IO_DATA_in(IO_DATA_in), .d0(d0), .d1(d1),
    .d2(d2), .d3(d3), .d4(d4), .IO_DATA_out(IO_DATA_out));
endmodule

module stack (
  input  CLK,
  input  RESET,
  input  [1:0] COMMAND,
  input  [2:0] INDEX,
  input  [3:0] IO_DATA_in,
  output [3:0] d0,
  output [3:0] d1,
  output [3:0] d2,
  output [3:0] d3,
  output [3:0] d4,
  output [3:0] IO_DATA_out
);

  wire and_1_out, not_1_out;
  wire [3:0] transmission_1_p1;

  and and_1 (and_1_out, COMMAND[0], not_1_out);
  not not_1 (not_1_out, COMMAND[1]);
  // Transmission_Gate #(.width(4)) transmission_1: pin names not known; wires that end beside it: transmission_1_p1, and_1_out, IO_DATA_in
  // NOT_Gate not_2 has open pins: in=and_1_out, out=open
  my_stack my_stack_1 (
    .I_DATA(IO_DATA_in), .RESET(RESET), .CLK(CLK), .COMMAND(COMMAND), .INDEX(INDEX),
    .O_DATA(transmission_1_p1), .d0(d0), .d1(d1), .d2(d2), .d3(d3), .d4(d4));

  assign IO_DATA_out = IO_DATA_in;
endmodule

module rs_trigger (
  input  R,
  input  CLK,
  input  S,
  input  RES,
  output Q,
  output inv_Q
);

  wire and_1_out, and_2_out, nor_2_out;

  and and_1 (and_1_out, R, CLK);
  and and_2 (and_2_out, CLK, S);
  nor nor_1 (Q, and_1_out, inv_Q);
  nor nor_2 (nor_2_out, Q, and_2_out);
  or or_1 (inv_Q, nor_2_out, RES);
endmodule

module d_trigger (
  input  CLK,
  input  D,
  input  RESET,
  output Q,
  output INV_Q
);

  wire not_1_out;

  not not_1 (not_1_out, D);
  rs_trigger rs_trigger_1 (.R(not_1_out), .CLK(CLK), .S(D), .RES(RESET), .Q(Q), .inv_Q(INV_Q));
endmodule

module multi_and (
  input  [3:0] I_DATA,
  input  KEY,
  output [3:0] RESULT
);

  and and_1 (RESULT[0], I_DATA[0], KEY);
  and and_2 (RESULT[1], I_DATA[1], KEY);
  and and_3 (RESULT[2], I_DATA[2], KEY);
  and and_4 (RESULT[3], I_DATA[3], KEY);
endmodule

module multi_or (
  input  [3:0] d0,
  input  [3:0] d1,
  input  [3:0] d2,
  input  [3:0] d3,
  input  [3:0] d4,
  output [3:0] Result
);

  or or_1 (Result[0], d0[0], d1[0], d2[0], d3[0], d4[0]);
  or or_2 (Result[1], d0[1], d1[1], d2[1], d3[1], d4[1]);
  or or_3 (Result[2], d0[2], d1[2], d2[2], d3[2], d4[2]);
  or or_4 (Result[3], d0[3], d1[3], d2[3], d3[3], d4[3]);
endmodule

module idx_converter (
  input  [2:0] ELEMENT_1,
  input  [2:0] ELEMENT_2,
  output [2:0] O_DATA
);

  wire and_1_out, and_2_out, and_3_out, and_4_out, and_5_out, and_6_out, and_7_out, and_8_out, and_9_out,
       and_10_out, and_11_out, and_12_out, and_13_out, and_14_out, and_15_out, and_16_out, and_17_out,
       and_18_out, and_19_out, and_20_out, and_21_out, and_22_out, and_23_out, and_24_out, and_25_out,
       and_26_out, and_27_out, and_28_out, and_29_out, and_30_out, and_31_out, and_32_out, and_33_out,
       and_34_out, and_35_out, and_36_out, and_37_out, and_38_out, and_39_out, and_40_out, check_0_1_o_data,
       check_0_2_o_data, check_1_1_o_data, check_1_2_o_data, check_2_1_o_data, check_2_2_o_data,
       check_3_1_o_data, check_3_2_o_data, check_4_1_o_data, check_4_2_o_data, not_1_out, not_2_out,
       not_3_out, not_4_out, not_5_out, not_6_out, not_7_out, not_8_out, not_9_out, not_10_out, or_1_out,
       or_2_out, or_3_out, or_4_out, or_5_out;

  check_0 check_0_1 (.I_DATA(ELEMENT_1), .O_DATA(check_0_1_o_data));
  check_1 check_1_1 (.I_DATA(ELEMENT_1), .O_DATA(check_1_1_o_data));
  check_2 check_2_1 (.I_DATA(ELEMENT_1), .O_DATA(check_2_1_o_data));
  check_3 check_3_1 (.I_DATA(ELEMENT_1), .O_DATA(check_3_1_o_data));
  check_4 check_4_1 (.I_DATA(ELEMENT_1), .O_DATA(check_4_1_o_data));
  check_0 check_0_2 (.I_DATA(ELEMENT_2), .O_DATA(check_0_2_o_data));
  check_1 check_1_2 (.I_DATA(ELEMENT_2), .O_DATA(check_1_2_o_data));
  check_2 check_2_2 (.I_DATA(ELEMENT_2), .O_DATA(check_2_2_o_data));
  check_3 check_3_2 (.I_DATA(ELEMENT_2), .O_DATA(check_3_2_o_data));
  check_4 check_4_2 (.I_DATA(ELEMENT_2), .O_DATA(check_4_2_o_data));
  and and_1 (and_1_out, check_0_1_o_data, check_0_2_o_data);
  and and_2 (and_2_out, check_0_1_o_data, check_1_2_o_data);
  and and_3 (and_3_out, check_0_1_o_data, check_2_2_o_data);
  and and_4 (and_4_out, check_0_1_o_data, check_3_2_o_data);
  and and_5 (and_5_out, check_0_1_o_data, check_4_2_o_data);
  and and_6 (and_6_out, check_1_1_o_data, check_0_2_o_data);
  and and_7 (and_7_out, check_1_1_o_data, check_1_2_o_data);
  and and_8 (and_8_out, check_1_1_o_data, check_2_2_o_data);
  and and_9 (and_9_out, check_1_1_o_data, check_3_2_o_data);
  and and_10 (and_10_out, check_1_1_o_data, check_4_2_o_data);
  and and_11 (and_11_out, check_2_1_o_data, check_0_2_o_data);
  and and_12 (and_12_out, check_2_1_o_data, check_1_2_o_data);
  and and_13 (and_13_out, check_2_1_o_data, check_2_2_o_data);
  and and_14 (and_14_out, check_2_1_o_data, check_3_2_o_data);
  and and_15 (and_15_out, check_2_1_o_data, check_4_2_o_data);
  and and_16 (and_16_out, check_3_1_o_data, check_0_2_o_data);
  and and_17 (and_17_out, check_3_1_o_data, check_1_2_o_data);
  and and_18 (and_18_out, check_3_1_o_data, check_2_2_o_data);
  and and_19 (and_19_out, check_3_1_o_data, check_3_2_o_data);
  and and_20 (and_20_out, check_3_1_o_data, check_4_2_o_data);
  and and_21 (and_21_out, check_4_1_o_data, check_0_2_o_data);
  and and_22 (and_22_out, check_4_1_o_data, check_1_2_o_data);
  and and_23 (and_23_out, check_4_1_o_data, check_2_2_o_data);
  and and_24 (and_24_out, check_4_1_o_data, check_3_2_o_data);
  and and_25 (and_25_out, check_4_1_o_data, check_4_2_o_data);
  or or_1 (or_1_out, and_1_out, and_7_out, and_13_out, and_19_out, and_25_out);
  or or_2 (or_2_out, and_5_out, and_6_out, and_12_out, and_18_out, and_24_out);
  or or_3 (or_3_out, and_4_out, and_10_out, and_11_out, and_17_out, and_23_out);
  or or_4 (or_4_out, and_3_out, and_9_out, and_15_out, and_16_out, and_22_out);
  or or_5 (or_5_out, and_14_out, and_21_out, and_20_out, and_2_out, and_8_out);
  not not_1 (not_1_out, 1'b1);
  not not_2 (not_2_out, 1'b1);
  not not_3 (not_3_out, 1'b1);
  not not_4 (not_4_out, 1'b1);
  not not_5 (not_5_out, 1'b1);
  not not_6 (not_6_out, 1'b1);
  not not_7 (not_7_out, 1'b1);
  not not_8 (not_8_out, 1'b1);
  not not_9 (not_9_out, 1'b1);
  not not_10 (not_10_out, 1'b1);
  and and_26 (and_26_out, not_1_out, or_1_out);
  and and_27 (and_27_out, not_2_out, or_1_out);
  and and_28 (and_28_out, not_3_out, or_1_out);
  and and_29 (and_29_out, 1'b1, or_2_out);
  and and_30 (and_30_out, not_4_out, or_2_out);
  and and_31 (and_31_out, not_5_out, or_2_out);
  and and_32 (and_32_out, not_6_out, or_3_out);
  and and_33 (and_33_out, 1'b1, or_3_out);
  and and_34 (and_34_out, not_7_out, or_3_out);
  and and_35 (and_35_out, 1'b1, or_4_out);
  and and_36 (and_36_out, 1'b1, or_4_out);
  and and_37 (and_37_out, not_8_out, or_4_out);
  and and_38 (and_38_out, not_9_out, or_5_out);
  and and_39 (and_39_out, not_10_out, or_5_out);
  and and_40 (and_40_out, 1'b1, or_5_out);
  or or_6 (O_DATA[0], and_26_out, and_29_out, and_32_out, and_35_out, and_38_out);
  or or_7 (O_DATA[1], and_27_out, and_33_out, and_30_out, and_36_out, and_39_out);
  or or_8 (O_DATA[2], and_28_out, and_31_out, and_34_out, and_37_out, and_40_out);
endmodule

module check_0 (
  input  [2:0] I_DATA,
  output O_DATA
);

  wire not_1_out, not_2_out, not_3_out;

  not not_1 (not_1_out, I_DATA[0]);
  not not_2 (not_2_out, I_DATA[1]);
  not not_3 (not_3_out, I_DATA[2]);
  and and_1 (O_DATA, not_1_out, not_2_out, not_3_out);
endmodule

module check_1 (
  input  [2:0] I_DATA,
  output O_DATA
);

  wire not_1_out, not_2_out;

  not not_1 (not_1_out, I_DATA[1]);
  not not_2 (not_2_out, I_DATA[2]);
  and and_1 (O_DATA, I_DATA[0], not_1_out, not_2_out);
endmodule

module check_2 (
  input  [2:0] I_DATA,
  output O_DATA
);

  wire not_1_out, not_2_out;

  not not_1 (not_1_out, I_DATA[0]);
  not not_2 (not_2_out, I_DATA[2]);
  and and_1 (O_DATA, not_1_out, I_DATA[1], not_2_out);
endmodule

module check_3 (
  input  [2:0] I_DATA,
  output O_DATA
);

  wire not_1_out;

  not not_1 (not_1_out, I_DATA[2]);
  and and_1 (O_DATA, I_DATA[0], I_DATA[1], not_1_out);
endmodule

module check_4 (
  input  [2:0] I_DATA,
  output O_DATA
);

  wire not_1_out, not_2_out;

  not not_1 (not_1_out, I_DATA[0]);
  not not_2 (not_2_out, I_DATA[1]);
  and and_1 (O_DATA, not_1_out, not_2_out, I_DATA[2]);
endmodule

module memory_4bits (
  input  RESET,
  input  CLK,
  input  KEY,
  input  [3:0] I_DATA,
  output [3:0] O_DATA
);

  wire and_1_out;

  and and_1 (and_1_out, CLK, KEY);
  d_trigger d_trigger_1 (.CLK(and_1_out), .D(I_DATA[0]), .RESET(RESET), .Q(O_DATA[0]));  // open: INV_Q
  d_trigger d_trigger_2 (.CLK(and_1_out), .D(I_DATA[1]), .RESET(RESET), .Q(O_DATA[1]));  // open: INV_Q
  d_trigger d_trigger_3 (.CLK(and_1_out), .D(I_DATA[2]), .RESET(RESET), .Q(O_DATA[2]));  // open: INV_Q
  d_trigger d_trigger_4 (.CLK(and_1_out), .D(I_DATA[3]), .RESET(RESET), .Q(O_DATA[3]));  // open: INV_Q
endmodule

module rs_trigger_jk (
  input  R,
  input  CLK,
  input  S,
  input  RESET,
  output Q,
  output INV_Q
);

  wire and_1_out, and_2_out, nor_1_out;

  and and_1 (and_1_out, R, CLK);
  and and_2 (and_2_out, CLK, S);
  nor nor_1 (nor_1_out, and_1_out, INV_Q);
  or or_1 (Q, nor_1_out, RESET);
  nor nor_2 (INV_Q, Q, and_2_out);
endmodule

module jk_trigger (
  input  K,
  input  CLK,
  input  J,
  input  RESET,
  output Q,
  output INV_Q
);

  wire and_1_out, and_2_out, not_1_out, rs_trigger_jk_1_inv_q, rs_trigger_jk_1_q;

  and and_1 (and_1_out, Q, K);
  and and_2 (and_2_out, J, INV_Q);
  rs_trigger_jk rs_trigger_jk_1 (
    .R(and_1_out), .CLK(CLK), .S(and_2_out), .RESET(RESET), .Q(rs_trigger_jk_1_q),
    .INV_Q(rs_trigger_jk_1_inv_q));
  not not_1 (not_1_out, CLK);
  rs_trigger_jk rs_trigger_jk_2 (
    .R(rs_trigger_jk_1_inv_q), .CLK(not_1_out), .S(rs_trigger_jk_1_q), .RESET(RESET), .Q(Q), .INV_Q(INV_Q));
endmodule

module jk_counter (
  input  CLK,
  input  RESET,
  output [2:0] O_DATA
);

  wire and_1_out, not_1_out, or_1_out;

  not not_1 (not_1_out, O_DATA[1]);
  and and_1 (and_1_out, O_DATA[0], not_1_out, O_DATA[2]);
  or or_1 (or_1_out, and_1_out, RESET);
  jk_trigger jk_trigger_1 (.K(1'b1), .CLK(CLK), .J(1'b1), .RESET(or_1_out), .INV_Q(O_DATA[0]));  // open: Q
  jk_trigger jk_trigger_2 (.K(1'b1), .CLK(O_DATA[0]), .J(1'b1), .RESET(or_1_out), .INV_Q(O_DATA[1]));  // open: Q
  jk_trigger jk_trigger_3 (.K(1'b1), .CLK(O_DATA[1]), .J(1'b1), .RESET(or_1_out), .INV_Q(O_DATA[2]));  // open: Q
endmodule

module \checker  (
  input  AND_1,
  input  AND_2,
  input  OR_1,
  output RESULT
);

  wire and_1_out;

  and u_and_1 (and_1_out, AND_1, AND_2);
  or u_or_1 (RESULT, and_1_out, OR_1);
endmodule

module idx_converter_negative (
  input  [2:0] I_DATA,
  output [2:0] O_DATA
);

  wire and_1_out, and_2_out, and_3_out, and_4_out, and_5_out, and_6_out, and_7_out, and_8_out, and_9_out,
       and_10_out, and_11_out, and_12_out, and_13_out, and_14_out, and_15_out, check_0_1_o_data,
       check_1_1_o_data, check_2_1_o_data, check_3_1_o_data, check_4_1_o_data, not_1_out, not_2_out,
       not_3_out, not_4_out, not_5_out, not_6_out, not_7_out, not_8_out, not_9_out, not_10_out;

  not not_1 (not_1_out, 1'b1);
  not not_2 (not_2_out, 1'b1);
  check_1 check_1_1 (.I_DATA(I_DATA), .O_DATA(check_1_1_o_data));
  not not_3 (not_3_out, 1'b1);
  not not_4 (not_4_out, 1'b1);
  check_2 check_2_1 (.I_DATA(I_DATA), .O_DATA(check_2_1_o_data));
  not not_5 (not_5_out, 1'b1);
  not not_6 (not_6_out, 1'b1);
  check_3 check_3_1 (.I_DATA(I_DATA), .O_DATA(check_3_1_o_data));
  not not_7 (not_7_out, 1'b1);
  check_4 check_4_1 (.I_DATA(I_DATA), .O_DATA(check_4_1_o_data));
  not not_8 (not_8_out, 1'b1);
  not not_9 (not_9_out, 1'b1);
  not not_10 (not_10_out, 1'b1);
  check_0 check_0_1 (.I_DATA(I_DATA), .O_DATA(check_0_1_o_data));
  and and_1 (and_1_out, not_1_out, check_1_1_o_data);
  and and_2 (and_2_out, not_2_out, check_1_1_o_data);
  and and_3 (and_3_out, not_3_out, check_1_1_o_data);
  and and_4 (and_4_out, 1'b1, check_2_1_o_data);
  and and_5 (and_5_out, not_4_out, check_2_1_o_data);
  and and_6 (and_6_out, not_5_out, check_2_1_o_data);
  and and_7 (and_7_out, not_6_out, check_3_1_o_data);
  and and_8 (and_8_out, 1'b1, check_3_1_o_data);
  and and_9 (and_9_out, not_7_out, check_3_1_o_data);
  and and_10 (and_10_out, 1'b1, check_4_1_o_data);
  and and_11 (and_11_out, 1'b1, check_4_1_o_data);
  and and_12 (and_12_out, not_8_out, check_4_1_o_data);
  and and_13 (and_13_out, not_9_out, check_0_1_o_data);
  and and_14 (and_14_out, not_10_out, check_0_1_o_data);
  and and_15 (and_15_out, 1'b1, check_0_1_o_data);
  or or_1 (O_DATA[0], and_1_out, and_4_out, and_7_out, and_10_out, and_13_out);
  or or_2 (O_DATA[1], and_2_out, and_8_out, and_5_out, and_11_out, and_14_out);
  or or_3 (O_DATA[2], and_3_out, and_6_out, and_9_out, and_12_out, and_15_out);
endmodule

module idx_mod_5 (
  input  [2:0] I_DATA,
  output [2:0] O_DATA
);

  wire and_1_out, and_2_out, and_3_out, and_4_out, and_5_out, and_6_out, and_7_out, and_8_out, and_9_out,
       and_10_out, and_11_out, and_12_out, and_13_out, and_14_out, and_15_out, and_16_out, and_17_out,
       and_18_out, check_0_1_o_data, check_1_1_o_data, check_2_1_o_data, check_3_1_o_data, check_4_1_o_data,
       not_1_out, not_2_out, not_3_out, not_4_out, not_5_out, not_6_out, not_7_out, not_8_out, not_9_out,
       not_10_out, not_11_out, not_12_out, or_1_out, or_2_out, or_3_out;

  not not_1 (not_1_out, I_DATA[1]);
  not not_2 (not_2_out, I_DATA[0]);
  check_0 check_0_1 (.I_DATA(I_DATA), .O_DATA(check_0_1_o_data));
  check_1 check_1_1 (.I_DATA(I_DATA), .O_DATA(check_1_1_o_data));
  check_2 check_2_1 (.I_DATA(I_DATA), .O_DATA(check_2_1_o_data));
  check_3 check_3_1 (.I_DATA(I_DATA), .O_DATA(check_3_1_o_data));
  check_4 check_4_1 (.I_DATA(I_DATA), .O_DATA(check_4_1_o_data));
  and and_1 (and_1_out, I_DATA[0], not_1_out, I_DATA[2]);
  and and_2 (and_2_out, not_2_out, I_DATA[1], I_DATA[2]);
  and and_3 (and_3_out, I_DATA[0], I_DATA[1], I_DATA[2]);
  not not_3 (not_3_out, 1'b1);
  not not_4 (not_4_out, 1'b1);
  not not_5 (not_5_out, 1'b1);
  or or_1 (or_1_out, check_0_1_o_data, and_1_out);
  not not_6 (not_6_out, 1'b1);
  or or_2 (or_2_out, and_2_out, check_1_1_o_data);
  not not_7 (not_7_out, 1'b1);
  not not_8 (not_8_out, 1'b1);
  or or_3 (or_3_out, and_3_out, check_2_1_o_data);
  not not_9 (not_9_out, 1'b1);
  not not_10 (not_10_out, 1'b1);
  not not_11 (not_11_out, 1'b1);
  not not_12 (not_12_out, 1'b1);
  and and_4 (and_4_out, not_3_out, or_1_out);
  and and_5 (and_5_out, not_4_out, or_1_out);
  and and_6 (and_6_out, not_5_out, or_1_out);
  and and_7 (and_7_out, 1'b1, or_2_out);
  and and_8 (and_8_out, not_6_out, or_2_out);
  and and_9 (and_9_out, not_7_out, or_2_out);
  and and_10 (and_10_out, not_8_out, or_3_out);
  and and_11 (and_11_out, 1'b1, or_3_out);
  and and_12 (and_12_out, not_9_out, or_3_out);
  and and_13 (and_13_out, 1'b1, check_3_1_o_data);
  and and_14 (and_14_out, 1'b1, check_3_1_o_data);
  and and_15 (and_15_out, not_10_out, check_3_1_o_data);
  and and_16 (and_16_out, not_11_out, check_4_1_o_data);
  and and_17 (and_17_out, not_12_out, check_4_1_o_data);
  and and_18 (and_18_out, 1'b1, check_4_1_o_data);
  or or_4 (O_DATA[0], and_4_out, and_7_out, and_10_out, and_13_out, and_16_out);
  or or_5 (O_DATA[1], and_5_out, and_11_out, and_8_out, and_14_out, and_17_out);
  or or_6 (O_DATA[2], and_6_out, and_9_out, and_12_out, and_15_out, and_18_out);
endmodule

module my_stack (
  input  [3:0] I_DATA,
  input  RESET,
  input  CLK,
  input  [1:0] COMMAND,
  input  [2:0] INDEX,
  output [3:0] O_DATA,
  output [3:0] d0,
  output [3:0] d1,
  output [3:0] d2,
  output [3:0] d3,
  output [3:0] d4
);

  wire and_1_out, and_2_out, and_3_out, and_4_out, and_5_out, and_6_out, and_7_out, and_8_out,
       check_0_1_o_data, check_0_2_o_data, check_0_3_o_data, check_1_1_o_data, check_1_2_o_data,
       check_1_3_o_data, check_2_1_o_data, check_2_2_o_data, check_2_3_o_data, check_3_1_o_data,
       check_3_2_o_data, check_3_3_o_data, check_4_1_o_data, check_4_2_o_data, check_4_3_o_data,
       checker_1_result, checker_2_result, checker_3_result, checker_4_result, checker_5_result, not_1_out,
       not_2_out;
  wire [2:0] idx_converter_1_o_data, idx_converter_2_o_data, idx_converter_negative_1_o_data,
       idx_mod_5_1_o_data, jk_counter_1_o_data, jk_counter_2_o_data;
  wire [3:0] multi_and_1_result, multi_and_2_result, multi_and_3_result, multi_and_4_result,
       multi_and_5_result;

  not not_1 (not_1_out, COMMAND[1]);
  not not_2 (not_2_out, COMMAND[0]);
  idx_mod_5 idx_mod_5_1 (.I_DATA(INDEX), .O_DATA(idx_mod_5_1_o_data));
  check_0 check_0_1 (.I_DATA(idx_converter_1_o_data), .O_DATA(check_0_1_o_data));
  check_1 check_1_1 (.I_DATA(idx_converter_1_o_data), .O_DATA(check_1_1_o_data));
  check_2 check_2_1 (.I_DATA(idx_converter_1_o_data), .O_DATA(check_2_1_o_data));
  check_3 check_3_1 (.I_DATA(idx_converter_1_o_data), .O_DATA(check_3_1_o_data));
  check_4 check_4_1 (.I_DATA(idx_converter_1_o_data), .O_DATA(check_4_1_o_data));
  idx_converter idx_converter_1 (
    .ELEMENT_1(idx_converter_negative_1_o_data), .ELEMENT_2(idx_mod_5_1_o_data),
    .O_DATA(idx_converter_1_o_data));
  jk_counter jk_counter_1 (.CLK(and_1_out), .RESET(RESET), .O_DATA(jk_counter_1_o_data));
  jk_counter jk_counter_2 (.CLK(and_2_out), .RESET(RESET), .O_DATA(jk_counter_2_o_data));
  idx_converter idx_converter_2 (
    .ELEMENT_1(jk_counter_1_o_data), .ELEMENT_2(jk_counter_2_o_data), .O_DATA(idx_converter_2_o_data));
  idx_converter_negative idx_converter_negative_1 (
    .I_DATA(idx_converter_2_o_data), .O_DATA(idx_converter_negative_1_o_data));
  and and_1 (and_1_out, COMMAND[0], CLK, not_1_out);
  and and_2 (and_2_out, not_2_out, CLK, COMMAND[1]);
  and and_3 (and_3_out, CLK, COMMAND[0], COMMAND[1]);
  check_0 check_0_2 (.I_DATA(idx_converter_2_o_data), .O_DATA(check_0_2_o_data));
  and and_4 (and_4_out, and_3_out, check_0_1_o_data);
  check_1 check_1_2 (.I_DATA(idx_converter_2_o_data), .O_DATA(check_1_2_o_data));
  and and_5 (and_5_out, and_3_out, check_1_1_o_data);
  check_2 check_2_2 (.I_DATA(idx_converter_2_o_data), .O_DATA(check_2_2_o_data));
  and and_6 (and_6_out, check_2_1_o_data, and_3_out);
  check_3 check_3_2 (.I_DATA(idx_converter_2_o_data), .O_DATA(check_3_2_o_data));
  and and_7 (and_7_out, and_3_out, check_3_1_o_data);
  check_4 check_4_2 (.I_DATA(idx_converter_2_o_data), .O_DATA(check_4_2_o_data));
  and and_8 (and_8_out, and_3_out, check_4_1_o_data);
  memory_4bits memory_4bits_1 (.RESET(RESET), .CLK(and_1_out), .KEY(check_0_2_o_data), .I_DATA(I_DATA), .O_DATA(d0));
  check_0 check_0_3 (.I_DATA(idx_converter_negative_1_o_data), .O_DATA(check_0_3_o_data));
  \checker  checker_1 (.AND_1(and_2_out), .AND_2(check_0_3_o_data), .OR_1(and_4_out), .RESULT(checker_1_result));
  memory_4bits memory_4bits_2 (.RESET(RESET), .CLK(and_1_out), .KEY(check_1_2_o_data), .I_DATA(I_DATA), .O_DATA(d1));
  check_1 check_1_3 (.I_DATA(idx_converter_negative_1_o_data), .O_DATA(check_1_3_o_data));
  \checker  checker_2 (.AND_1(and_2_out), .AND_2(check_1_3_o_data), .OR_1(and_5_out), .RESULT(checker_2_result));
  memory_4bits memory_4bits_3 (.RESET(RESET), .CLK(and_1_out), .KEY(check_2_2_o_data), .I_DATA(I_DATA), .O_DATA(d2));
  check_2 check_2_3 (.I_DATA(idx_converter_negative_1_o_data), .O_DATA(check_2_3_o_data));
  \checker  checker_3 (.AND_1(and_2_out), .AND_2(check_2_3_o_data), .OR_1(and_6_out), .RESULT(checker_3_result));
  memory_4bits memory_4bits_4 (.RESET(RESET), .CLK(and_1_out), .KEY(check_3_2_o_data), .I_DATA(I_DATA), .O_DATA(d3));
  check_3 check_3_3 (.I_DATA(idx_converter_negative_1_o_data), .O_DATA(check_3_3_o_data));
  \checker  checker_4 (.AND_1(and_2_out), .AND_2(check_3_3_o_data), .OR_1(and_7_out), .RESULT(checker_4_result));
  memory_4bits memory_4bits_5 (.RESET(RESET), .CLK(and_1_out), .KEY(check_4_2_o_data), .I_DATA(I_DATA), .O_DATA(d4));
  check_4 check_4_3 (.I_DATA(idx_converter_negative_1_o_data), .O_DATA(check_4_3_o_data));
  \checker  checker_5 (.AND_1(and_2_out), .AND_2(check_4_3_o_data), .OR_1(and_8_out), .RESULT(checker_5_result));
  multi_and multi_and_1 (.I_DATA(d0), .KEY(checker_1_result), .RESULT(multi_and_1_result));
  multi_and multi_and_2 (.I_DATA(d1), .KEY(checker_2_result), .RESULT(multi_and_2_result));
  multi_and multi_and_3 (.I_DATA(d2), .KEY(checker_3_result), .RESULT(multi_and_3_result));
  multi_and multi_and_4 (.I_DATA(d3), .KEY(checker_4_result), .RESULT(multi_and_4_result));
  multi_and multi_and_5 (.I_DATA(d4), .KEY(checker_5_result), .RESULT(multi_and_5_result));
  multi_or multi_or_1 (
    .d0(multi_and_1_result), .d1(multi_and_2_result), .d2(multi_and_3_result), .d3(multi_and_4_result),
    .d4(multi_and_5_result), .Result(O_DATA));
endmodule
